// Logisim project PROJECT.circ as structural Verilog: 10 circuits, main circuit main
// ↓
module main (
  input  in_1
);

  wire button_2_out, button_3_out, button_4_out, button_out, R_out;
  wire [1:0] joystick_1_y;
  wire [3:0] to_10_notation_1_out_2, to_10_notation_1_out_3, to_10_notation_2_out_2, to_10_notation_2_out_3,
       to_10_notation_3_out_2, to_10_notation_3_out_3, to_10_notation_4_out_2, to_10_notation_4_out_3;
  wire [4:0] kinematic_chip_1_ball_x, kinematic_chip_1_ball_y, kinematic_chip_1_player_bat_out,
       kinematic_chip_1_robot_bat_out;
  wire [7:0] kinematic_chip_1_player_score, kinematic_chip_1_robot_score, kinematic_chip_1_robot_speed,
       kinematic_chip_1_win_score;
  wire [31:0] full_video_chip_1_out_5, full_video_chip_1_out_6, full_video_chip_1_out_7,
       full_video_chip_1_out_8, full_video_chip_1_out_9, full_video_chip_1_out_10, full_video_chip_1_out_11,
       full_video_chip_1_out_12, full_video_chip_1_out_13, full_video_chip_1_out_14,
       full_video_chip_1_out_15, full_video_chip_1_out_16, full_video_chip_1_out_17,
       full_video_chip_1_out_18, full_video_chip_1_out_19, full_video_chip_1_out_20,
       full_video_chip_1_out_21, full_video_chip_1_out_22, full_video_chip_1_out_23,
       full_video_chip_1_out_24, full_video_chip_1_out_25, full_video_chip_1_out_26,
       full_video_chip_1_out_27, full_video_chip_1_out_28, full_video_chip_1_out_29,
       full_video_chip_1_out_30, full_video_chip_1_out_31, full_video_chip_1_out_32,
       full_video_chip_1_out_33, full_video_chip_1_out_34, full_video_chip_1_out_35, full_video_chip_1_out_36;

  Joystick #(.bits(2)) joystick_1 (.y(joystick_1_y));  // open: x
  DotMatrix #(.matrixcols(32), .matrixrows(32)) dotmatrix_1 (
    .col0(full_video_chip_1_out_5), .col1(full_video_chip_1_out_6), .col2(full_video_chip_1_out_7),
    .col3(full_video_chip_1_out_8), .col4(full_video_chip_1_out_9), .col5(full_video_chip_1_out_10),
    .col6(full_video_chip_1_out_11), .col7(full_video_chip_1_out_12), .col8(full_video_chip_1_out_13),
    .col9(full_video_chip_1_out_14), .col10(full_video_chip_1_out_15), .col11(full_video_chip_1_out_16),
    .col12(full_video_chip_1_out_17), .col13(full_video_chip_1_out_18), .col14(full_video_chip_1_out_19),
    .col15(full_video_chip_1_out_20), .col16(full_video_chip_1_out_21), .col17(full_video_chip_1_out_22),
    .col18(full_video_chip_1_out_23), .col19(full_video_chip_1_out_24), .col20(full_video_chip_1_out_25),
    .col21(full_video_chip_1_out_26), .col22(full_video_chip_1_out_27), .col23(full_video_chip_1_out_28),
    .col24(full_video_chip_1_out_29), .col25(full_video_chip_1_out_30), .col26(full_video_chip_1_out_31),
    .col27(full_video_chip_1_out_32), .col28(full_video_chip_1_out_33), .col29(full_video_chip_1_out_34),
    .col30(full_video_chip_1_out_35), .col31(full_video_chip_1_out_36));
  full_video_chip full_video_chip_1 (
    .X_ball(kinematic_chip_1_ball_x), .Y_ball(kinematic_chip_1_ball_y),
    .in_3(kinematic_chip_1_player_bat_out), .in_4(kinematic_chip_1_robot_bat_out),
    .out_5(full_video_chip_1_out_5), .out_6(full_video_chip_1_out_6), .out_7(full_video_chip_1_out_7),
    .out_8(full_video_chip_1_out_8), .out_9(full_video_chip_1_out_9), .out_10(full_video_chip_1_out_10),
    .out_11(full_video_chip_1_out_11), .out_12(full_video_chip_1_out_12), .out_13(full_video_chip_1_out_13),
    .out_14(full_video_chip_1_out_14), .out_15(full_video_chip_1_out_15), .out_16(full_video_chip_1_out_16),
    .out_17(full_video_chip_1_out_17), .out_18(full_video_chip_1_out_18), .out_19(full_video_chip_1_out_19),
    .out_20(full_video_chip_1_out_20), .out_21(full_video_chip_1_out_21), .out_22(full_video_chip_1_out_22),
    .out_23(full_video_chip_1_out_23), .out_24(full_video_chip_1_out_24), .out_25(full_video_chip_1_out_25),
    .out_26(full_video_chip_1_out_26), .out_27(full_video_chip_1_out_27), .out_28(full_video_chip_1_out_28),
    .out_29(full_video_chip_1_out_29), .out_30(full_video_chip_1_out_30), .out_31(full_video_chip_1_out_31),
    .out_32(full_video_chip_1_out_32), .out_33(full_video_chip_1_out_33), .out_34(full_video_chip_1_out_34),
    .out_35(full_video_chip_1_out_35), .out_36(full_video_chip_1_out_36));
  Button R (.out(R_out));
  Button button (.out(button_out));
  Button button_2 (.out(button_2_out));
  Hex_Digit_Display hex_digit_display_1 (.value(to_10_notation_2_out_2));  // open: dp
  to_10_notation to_10_notation_1 (
    .in_1(kinematic_chip_1_win_score), .out_2(to_10_notation_1_out_2), .out_3(to_10_notation_1_out_3));
  Hex_Digit_Display hex_digit_display_2 (.value(to_10_notation_1_out_3));  // open: dp
  Hex_Digit_Display hex_digit_display_3 (.value(to_10_notation_1_out_2));  // open: dp
  kinematic_chip kinematic_chip_1 (
    .Joystik(joystick_1_y), .Reset(R_out), .Player_bat_out(kinematic_chip_1_player_bat_out),
    .ball_Y(kinematic_chip_1_ball_y), .ball_X(kinematic_chip_1_ball_x),
    .Player_score(kinematic_chip_1_player_score), .Robot_score(kinematic_chip_1_robot_score), .Pause(in_1),
    .Down(button_2_out), .Win_score(kinematic_chip_1_win_score), .Up(button_out), .Up_2(button_3_out),
    .Down_2(button_4_out), .Robot_speed(kinematic_chip_1_robot_speed),
    .Robot_bat_out(kinematic_chip_1_robot_bat_out));
  to_10_notation to_10_notation_2 (
    .in_1(kinematic_chip_1_player_score), .out_2(to_10_notation_2_out_2), .out_3(to_10_notation_2_out_3));
  Hex_Digit_Display hex_digit_display_4 (.value(to_10_notation_2_out_3));  // open: dp
  to_10_notation to_10_notation_3 (
    .in_1(kinematic_chip_1_robot_score), .out_2(to_10_notation_3_out_2), .out_3(to_10_notation_3_out_3));
  Hex_Digit_Display hex_digit_display_5 (.value(to_10_notation_3_out_3));  // open: dp
  Hex_Digit_Display hex_digit_display_6 (.value(to_10_notation_3_out_2));  // open: dp
  Hex_Digit_Display hex_digit_display_7 (.value(to_10_notation_4_out_2));  // open: dp
  Button button_3 (.out(button_3_out));
  Button button_4 (.out(button_4_out));
  Hex_Digit_Display hex_digit_display_8 (.value(to_10_notation_4_out_3));  // open: dp
  to_10_notation to_10_notation_4 (
    .in_1(kinematic_chip_1_robot_speed), .out_2(to_10_notation_4_out_2), .out_3(to_10_notation_4_out_3));

  // Notes on the sheet:
  //   Bat
  //   control
  //   Win score
  //   Player score
  //   Robot score
  //   Robot speed
endmodule

module kinematic_chip (
  input  Reset,
  input  Pause,
  input  [1:0] Joystik,
  input  Up,
  input  Up_2,
  input  Down,
  input  Down_2,
  output [4:0] Player_bat_out,
  output [4:0] Robot_bat_out,
  output [4:0] ball_Y,
  output [4:0] ball_X,
  output [7:0] Player_score,
  output [7:0] Robot_score,
  output [7:0] Win_score,
  output [7:0] Robot_speed
);

  wire adder_2_cout, adder_13_cout, and_2_out, and_4_out, and_8_out, and_9_out, and_10_out, and_11_out,
       BALL_TCT, BAT_TCT, BOT_TCT, clock_1_out, clock_2_out, clock_3_out, clock_4_out, clock_5_out,
       comparator_1_lt, comparator_2_lt, comparator_3_eq, comparator_3_gt, comparator_4_eq, comparator_5_eq,
       comparator_6_eq, comparator_7_eq, comparator_8_eq, comparator_9_eq, comparator_10_eq,
       comparator_11_eq, comparator_12_eq, comparator_13_eq, comparator_14_eq, comparator_15_lt,
       comparator_16_eq, comparator_17_eq, comparator_18_eq, comparator_19_eq, comparator_20_gt,
       comparator_20_lt, comparator_21_eq, comparator_22_eq, comparator_23_eq, comparator_24_eq,
       comparator_25_eq, comparator_26_eq, comparator_27_lt, comparator_28_eq, comparator_29_eq,
       comparator_30_gt, comparator_31_eq, comparator_31_gt, comparator_32_eq, comparator_32_lt,
       comparator_33_gt, Game_status, not_1_out, not_2_out, not_3_out, not_4_out, not_5_out, not_6_out,
       not_7_out, not_8_out, not_9_out, not_10_out, not_11_out, not_12_out, not_13_out, not_14_out,
       not_15_out, not_16_out, OPT_TCT, or_1_out, or_2_out, or_4_out, or_5_out, or_8_out, or_9_out, PAUSE_t,
       Player_hit, Player_win, Robot_hit, Robot_win, TCT, Wall_hit, xnor_1_out, xor_1_out, xor_2_out;
  wire [1:0] multiplexer_27_out, multiplexer_29_out;
  wire [2:0] _8_bit_X, _8_bit_Y, adder_3_out, multiplexer_1_out, multiplexer_2_out, multiplexer_8_out,
       multiplexer_9_out, multiplexer_10_out, multiplexer_12_out, multiplexer_13_out, multiplexer_17_out,
       multiplexer_19_out, multiplexer_28_out, negator_1_out, negator_2_out, negator_3_out, negator_4_out,
       negator_5_out, negator_6_out, negator_7_out, New_vY, subtractor_3_out, vX;
  wire [4:0] adder_1_out, adder_8_out, adder_9_out, adder_10_out, adder_11_out, adder_12_out,
       multiplexer_3_out, multiplexer_4_out, multiplexer_15_out, multiplexer_16_out, multiplexer_25_out,
       multiplexer_26_out, multiplexer_30_out, multiplexer_31_out, robot_chip_1_ball_y_predict,
       subtractor_1_out, subtractor_6_out;
  wire [5:3] vXY;
  wire [7:0] adder_2_out, adder_4_out, adder_5_out, adder_6_out, adder_7_out, adder_13_out, counter_1_q,
       divider_1_rem, multiplexer_6_out, multiplexer_7_out, multiplexer_11_out, multiplexer_14_out,
       multiplexer_21_out, multiplexer_22_out, multiplexer_23_out, multiplexer_24_out, multiplier_1_out,
       n8_bit_reg_1_out, n8_bit_reg_4_out, Robot_speed_t, subtractor_2_out, subtractor_4_out;

  Clock #(.highDuration(9), .lowDuration(9)) clock_1 (.out(clock_1_out));
  Clock clock_2 (.out(clock_2_out));
  _5_bit_reg u_5_bit_reg_1 (
    .In(multiplexer_16_out), .Reset_value(5'b01110), .out_5(Player_bat_out), .in_3(Reset), .in_4(BAT_TCT));
  and and_1 (TCT, clock_1_out, not_1_out);
  not not_1 (not_1_out, PAUSE_t);
  and and_2 (and_2_out, clock_2_out, not_2_out);
  not not_2 (not_2_out, PAUSE_t);
  Multiplier multiplier_1 (.a(Robot_speed_t), .b(8'h3), .out(multiplier_1_out));  // open: cin, cout
  Adder #(.width(5)) adder_1 (.a(Player_bat_out), .b(5'b00001), .out(adder_1_out));  // open: cin, cout
  Subtractor #(.width(5)) subtractor_1 (.a(Player_bat_out), .b(5'b00001), .out(subtractor_1_out));  // open: bin, bout
  Negator #(.width(3)) negator_1 (.in(vXY), .out(negator_1_out));
  _3_bit_reg u_3_bit_reg_1 (.In(multiplexer_8_out), .Reset_value(3'b011), .out_5(vXY), .in_3(Reset), .in_4(BALL_TCT));
  Negator #(.width(3)) negator_2 (.in(vXY), .out(negator_2_out));
  Negator #(.width(3)) negator_3 (.in(vXY), .out(negator_3_out));
  Comparator #(.width(3)) comparator_1 (.a(vXY), .b(3'b000), .lt(comparator_1_lt));  // open: gt, eq
  Negator #(.width(3)) negator_4 (.in(vXY), .out(negator_4_out));
  Comparator #(.width(3)) comparator_2 (.a(vXY), .b(3'b000), .lt(comparator_2_lt));  // open: gt, eq
  Comparator #(.width(3)) comparator_3 (.a(vXY), .b(3'b000), .gt(comparator_3_gt), .eq(comparator_3_eq));  // open: lt
  or or_1 (or_1_out, comparator_3_gt, comparator_3_eq);
  Comparator #(.width(2)) comparator_4 (.a(Joystik), .b(2'b01), .eq(comparator_4_eq));  // open: gt, lt
  _8_bit_reg u_8_bit_reg_1 (
    .In(Player_score), .Reset_value({8{1'b0}}), .Reset(Reset), .Tacts(BALL_TCT), .out(n8_bit_reg_1_out));
  _8_bit_reg u_8_bit_reg_2 (
    .In(multiplexer_14_out), .Reset_value(8'ha), .Reset(Reset), .Tacts(OPT_TCT), .out(Win_score));
  Counter counter_1 (.load(1'b0), .D({8{1'b0}}), .Q(counter_1_q), .clk(and_2_out));  // open: count, carry, clr
  Divider divider_1 (.a(counter_1_q), .b(multiplier_1_out), .rem(divider_1_rem));  // open: out, upper
  Comparator #(.width(5)) comparator_5 (.a(5'b11110), .b(adder_1_out), .eq(comparator_5_eq));  // open: gt, lt
  Comparator #(.width(5)) comparator_6 (.a(subtractor_1_out), .b({5{1'b1}}), .eq(comparator_6_eq));  // open: gt, lt
  Adder adder_2 (
    .a({ball_Y, _8_bit_Y}), .b({{6{vXY[5]}}, vXY[4:3]}), .out(adder_2_out), .cout(adder_2_cout));  // open: cin
  Multiplexer #(.width(3), .enable("false")) multiplexer_1 (
    .in0(vXY), .in1(negator_3_out), .out(multiplexer_1_out), .sel(comparator_1_lt));
  Adder #(.width(3)) adder_3 (.a(multiplexer_1_out), .b(3'b001), .out(adder_3_out));  // open: cin, cout
  Multiplexer #(.width(3), .enable("false")) multiplexer_2 (
    .in0(vXY), .in1(negator_4_out), .out(multiplexer_2_out), .sel(comparator_2_lt));
  Adder adder_4 (.a(n8_bit_reg_1_out), .b(8'h1), .out(adder_4_out));  // open: cin, cout
  Comparator #(.width(5)) comparator_7 (.a(ball_X), .b({5{1'b1}}), .eq(comparator_7_eq));  // open: gt, lt
  Adder adder_5 (.a(Win_score), .b(8'h1), .out(adder_5_out));  // open: cin, cout
  Subtractor subtractor_2 (.a(Win_score), .b(8'h1), .out(subtractor_2_out));  // open: bin, bout
  Clock #(.highDuration(6), .lowDuration(6)) clock_3 (.out(clock_3_out));
  and and_3 (BALL_TCT, clock_3_out, not_3_out);
  not not_3 (not_3_out, PAUSE_t);
  Comparator comparator_8 (.a(divider_1_rem), .b({8{1'b0}}), .eq(comparator_8_eq));  // open: gt, lt
  Multiplexer #(.width(5), .enable("false")) multiplexer_3 (
    .in0(Player_bat_out), .in1(adder_1_out), .out(multiplexer_3_out), .sel(not_4_out));
  not not_4 (not_4_out, comparator_5_eq);
  Multiplexer #(.width(5), .enable("false")) multiplexer_4 (
    .in0(subtractor_1_out), .in1(Player_bat_out), .out(multiplexer_4_out), .sel(comparator_6_eq));
  _8_bit_reg u_8_bit_reg_3 (
    .In(adder_2_out), .Reset_value(8'h80), .Reset(Reset), .Tacts(TCT), .out({ball_Y, _8_bit_Y}));
  Comparator #(.width(3)) comparator_9 (.a(3'b100), .b(adder_3_out), .eq(comparator_9_eq));  // open: gt, lt
  Subtractor #(.width(3)) subtractor_3 (.a(multiplexer_2_out), .b(3'b001), .out(subtractor_3_out));  // open: bin, bout
  Comparator #(.width(3)) comparator_10 (.a(3'b111), .b(subtractor_3_out), .eq(comparator_10_eq));  // open: gt, lt
  xnor xnor_1 (xnor_1_out, or_1_out, comparator_4_eq);
  Multiplexer #(.width(8), .enable("false")) multiplexer_5 (
    .in0(n8_bit_reg_1_out), .in1(adder_4_out), .out(Player_score), .sel(and_4_out));
  and and_4 (and_4_out, Wall_hit, comparator_7_eq);
  Multiplexer #(.width(8), .enable("false")) multiplexer_6 (
    .in0(Win_score), .in1(adder_5_out), .out(multiplexer_6_out), .sel(not_5_out));
  not not_5 (not_5_out, comparator_11_eq);
  Comparator comparator_11 (.a(8'h64), .b(adder_5_out), .eq(comparator_11_eq));  // open: gt, lt
  Comparator comparator_12 (.a(subtractor_2_out), .b({8{1'b0}}), .eq(comparator_12_eq));  // open: gt, lt
  Multiplexer #(.width(8), .enable("false")) multiplexer_7 (
    .in0(subtractor_2_out), .in1(Win_score), .out(multiplexer_7_out), .sel(comparator_12_eq));
  Counter #(.width(1), .max('h1)) counter_2 (
    .load(1'b0), .D(1'b0), .Q(BOT_TCT), .clk(comparator_8_eq));  // open: count, carry, clr
  Multiplexer #(.width(3), .enable("false")) multiplexer_8 (
    .in0(New_vY), .in1(negator_1_out), .out(multiplexer_8_out), .sel(xor_1_out));
  Multiplexer #(.width(3), .enable("false")) multiplexer_9 (
    .in0(negator_2_out), .in1(adder_3_out), .out(multiplexer_9_out), .sel(not_6_out));
  not not_6 (not_6_out, comparator_9_eq);
  Multiplexer #(.width(3), .enable("false")) multiplexer_10 (
    .in0(vXY), .in1(subtractor_3_out), .out(multiplexer_10_out), .sel(not_7_out));
  not not_7 (not_7_out, comparator_10_eq);
  Multiplexer #(.width(8), .enable("false")) multiplexer_11 (
    .in0(Win_score), .in1(multiplexer_6_out), .out(multiplexer_11_out), .sel(Up));
  Clock #(.highDuration(18), .lowDuration(18)) clock_4 (.out(clock_4_out));
  not not_8 (not_8_out, PAUSE_t);
  xor xor_1 (xor_1_out, vXY[5], adder_2_cout);
  Multiplexer #(.width(3), .enable("false")) multiplexer_12 (
    .in0(multiplexer_9_out), .in1(negator_5_out), .out(multiplexer_12_out), .sel(comparator_1_lt));
  Negator #(.width(3)) negator_5 (.in(multiplexer_9_out), .out(negator_5_out));
  Multiplexer #(.width(3), .enable("false")) multiplexer_13 (
    .in0(multiplexer_10_out), .in1(negator_6_out), .out(multiplexer_13_out), .sel(comparator_2_lt));
  Negator #(.width(3)) negator_6 (.in(multiplexer_10_out), .out(negator_6_out));
  Multiplexer #(.width(8), .enable("false")) multiplexer_14 (
    .in0(multiplexer_11_out), .in1(multiplexer_7_out), .out(multiplexer_14_out), .sel(Down));
  and and_5 (BAT_TCT, clock_4_out, not_8_out);
  not not_9 (not_9_out, Joystik[0]);
  Multiplexer #(.width(5), .enable("false")) multiplexer_15 (
    .in0(multiplexer_3_out), .in1(multiplexer_4_out), .out(multiplexer_15_out), .sel(Joystik[1]));
  Multiplexer #(.width(5), .enable("false")) multiplexer_16 (
    .in0(multiplexer_15_out), .in1(Player_bat_out), .out(multiplexer_16_out), .sel(not_9_out));
  Multiplexer #(.width(3), .enable("false")) multiplexer_17 (
    .in0(multiplexer_12_out), .in1(multiplexer_13_out), .out(multiplexer_17_out), .sel(xnor_1_out));
  Comparator #(.width(2)) comparator_13 (.a(Joystik), .b(2'b10), .eq(comparator_13_eq));  // open: gt, lt
  Multiplexer #(.width(3), .enable("false")) multiplexer_18 (
    .in0(vXY), .in1(multiplexer_19_out), .out(New_vY), .sel(Player_hit));
  Multiplexer #(.width(3), .enable("false")) multiplexer_19 (
    .in0(multiplexer_17_out), .in1(vXY), .out(multiplexer_19_out), .sel(comparator_13_eq));
  Clock #(.highDuration(50), .lowDuration(50)) clock_5 (.out(clock_5_out));
  and and_6 (OPT_TCT, clock_5_out, not_10_out);
  not not_10 (not_10_out, Game_status);
  not not_11 (not_11_out, Reset);
  and and_7 (PAUSE_t, not_11_out, or_2_out);
  or or_2 (or_2_out, Pause, Game_status);
  _8_bit_reg u_8_bit_reg_4 (
    .In(Robot_score), .Reset_value({8{1'b0}}), .Reset(Reset), .Tacts(BALL_TCT), .out(n8_bit_reg_4_out));
  _8_bit_reg u_8_bit_reg_5 (
    .In(multiplexer_24_out), .Reset_value(8'h5), .Reset(Reset), .Tacts(OPT_TCT), .out(Robot_speed));
  Adder adder_6 (.a(n8_bit_reg_4_out), .b(8'h1), .out(adder_6_out));  // open: cin, cout
  Comparator #(.width(5)) comparator_14 (.a(ball_X), .b({5{1'b0}}), .eq(comparator_14_eq));  // open: gt, lt
  Adder adder_7 (.a(Robot_speed), .b(8'h1), .out(adder_7_out));  // open: cin, cout
  Subtractor subtractor_4 (.a(Robot_speed), .b(8'h1), .out(subtractor_4_out));  // open: bin, bout
  Subtractor subtractor_5 (.a(8'hb), .b(Robot_speed), .out(Robot_speed_t));  // open: bin, bout
  // Probe on Robot_bat_out
  _5_bit_reg u_5_bit_reg_2 (
    .In(multiplexer_31_out), .Reset_value(5'b01110), .out_5(Robot_bat_out), .in_3(Reset), .in_4(and_8_out));
  and and_8 (and_8_out, comparator_15_lt, BOT_TCT);
  Comparator #(.width(5), .mode("unsigned")) comparator_15 (
    .a(ball_X), .b(5'b10001), .lt(comparator_15_lt));  // open: gt, eq
  _3_bit_reg u_3_bit_reg_2 (.In(multiplexer_28_out), .Reset_value(3'b110), .out_5(vX), .in_3(Reset), .in_4(BALL_TCT));
  Multiplexer #(.width(8), .enable("false")) multiplexer_20 (
    .in0(n8_bit_reg_4_out), .in1(adder_6_out), .out(Robot_score), .sel(and_9_out));
  and and_9 (and_9_out, Wall_hit, comparator_14_eq);
  Multiplexer #(.width(8), .enable("false")) multiplexer_21 (
    .in0(Robot_speed), .in1(adder_7_out), .out(multiplexer_21_out), .sel(not_12_out));
  not not_12 (not_12_out, comparator_16_eq);
  Comparator comparator_16 (.a(8'hb), .b(adder_7_out), .eq(comparator_16_eq));  // open: gt, lt
  Comparator comparator_17 (.a(subtractor_4_out), .b({8{1'b0}}), .eq(comparator_17_eq));  // open: gt, lt
  Multiplexer #(.width(8), .enable("false")) multiplexer_22 (
    .in0(subtractor_4_out), .in1(Robot_speed), .out(multiplexer_22_out), .sel(comparator_17_eq));
  Negator #(.width(3)) negator_7 (.in(vX), .out(negator_7_out));
  Adder #(.width(5)) adder_8 (.a(Player_bat_out), .b(5'b00001), .out(adder_8_out));  // open: cin, cout
  and and_10 (and_10_out, not_13_out, vX[2]);
  not not_13 (not_13_out, adder_13_cout);
  Multiplexer #(.width(8), .enable("false")) multiplexer_23 (
    .in0(Robot_speed), .in1(multiplexer_21_out), .out(multiplexer_23_out), .sel(Up_2));
  Robot_chip robot_chip_1 (
    .in_1(Reset), .Vxy({2'b00, vXY, vX}), .Ball_X({ball_X, _8_bit_X}), .Ball_Y({ball_Y, _8_bit_Y}),
    .Ball_Y_predict(robot_chip_1_ball_y_predict));
  // Probe on robot_chip_1_ball_y_predict
  Comparator #(.width(5)) comparator_18 (.a(5'b11110), .b(adder_9_out), .eq(comparator_18_eq));  // open: gt, lt
  Adder #(.width(5)) adder_9 (.a(Robot_bat_out), .b(5'b00001), .out(adder_9_out));  // open: cin, cout
  Comparator #(.width(5)) comparator_19 (.a(subtractor_6_out), .b({5{1'b1}}), .eq(comparator_19_eq));  // open: gt, lt
  Subtractor #(.width(5)) subtractor_6 (.a(Robot_bat_out), .b(5'b00001), .out(subtractor_6_out));  // open: bin, bout
  Adder #(.width(5)) adder_10 (.a(adder_8_out), .b(5'b00001), .out(adder_10_out));  // open: cin, cout
  Adder #(.width(5)) adder_11 (.a(Robot_bat_out), .b(5'b00001), .out(adder_11_out));  // open: cin, cout
  Adder #(.width(5)) adder_12 (.a(adder_11_out), .b(5'b00001), .out(adder_12_out));  // open: cin, cout
  or or_3 (Wall_hit, and_10_out, and_11_out);
  _8_bit_reg u_8_bit_reg_6 (
    .In(adder_13_out), .Reset_value(8'h80), .Reset(Reset), .Tacts(TCT), .out({ball_X, _8_bit_X}));
  Adder adder_13 (
    .a({ball_X, _8_bit_X}), .b({{6{vX[2]}}, vX[1:0]}), .out(adder_13_out), .cout(adder_13_cout));  // open: cin
  Multiplexer #(.width(8), .enable("false")) multiplexer_24 (
    .in0(multiplexer_23_out), .in1(multiplexer_22_out), .out(multiplexer_24_out), .sel(Down_2));
  Comparator #(.width(5), .mode("unsigned")) comparator_20 (
    .a(robot_chip_1_ball_y_predict), .b(Robot_bat_out), .gt(comparator_20_gt), .lt(comparator_20_lt));  // open: eq
  Multiplexer #(.width(5), .enable("false")) multiplexer_25 (
    .in0(Robot_bat_out), .in1(adder_9_out), .out(multiplexer_25_out), .sel(not_14_out));
  not not_14 (not_14_out, comparator_18_eq);
  Multiplexer #(.width(5), .enable("false")) multiplexer_26 (
    .in0(subtractor_6_out), .in1(Robot_bat_out), .out(multiplexer_26_out), .sel(comparator_19_eq));
  Comparator #(.width(5)) comparator_21 (.a(ball_Y), .b(Player_bat_out), .eq(comparator_21_eq));  // open: gt, lt
  Comparator #(.width(5)) comparator_22 (.a(ball_Y), .b(adder_8_out), .eq(comparator_22_eq));  // open: gt, lt
  Comparator #(.width(5)) comparator_23 (.a(ball_Y), .b(adder_10_out), .eq(comparator_23_eq));  // open: gt, lt
  Comparator #(.width(5)) comparator_24 (.a(ball_Y), .b(Robot_bat_out), .eq(comparator_24_eq));  // open: gt, lt
  Comparator #(.width(5)) comparator_25 (.a(ball_Y), .b(adder_11_out), .eq(comparator_25_eq));  // open: gt, lt
  Comparator #(.width(5)) comparator_26 (.a(ball_Y), .b(adder_12_out), .eq(comparator_26_eq));  // open: gt, lt
  and and_11 (and_11_out, adder_13_cout, not_15_out);
  not not_15 (not_15_out, vX[2]);
  Multiplexer #(.width(2), .enable("false")) multiplexer_27 (
    .in0(2'b10), .in1(2'b11), .out(multiplexer_27_out), .sel(comparator_20_lt));
  Multiplexer #(.width(3), .enable("false")) multiplexer_28 (
    .in0(vX), .in1(negator_7_out), .out(multiplexer_28_out), .sel(or_8_out));
  or or_4 (or_4_out, comparator_21_eq, comparator_22_eq, comparator_23_eq);
  or or_5 (or_5_out, comparator_24_eq, comparator_25_eq, comparator_26_eq);
  xor xor_2 (xor_2_out, vX[2], adder_13_cout);
  Multiplexer #(.width(2), .enable("false")) multiplexer_29 (
    .in0(multiplexer_27_out), .in1(2'b01), .out(multiplexer_29_out), .sel(comparator_20_gt));
  Comparator #(.width(3)) comparator_27 (.a(vX), .b(3'b000), .lt(comparator_27_lt));  // open: gt, eq
  Comparator #(.width(5)) comparator_28 (.a(5'b00100), .b(ball_X), .eq(comparator_28_eq));  // open: gt, lt
  Comparator #(.width(5)) comparator_29 (.a(ball_X), .b(5'b11011), .eq(comparator_29_eq));  // open: gt, lt
  Comparator #(.width(3)) comparator_30 (.a(vX), .b(3'b000), .gt(comparator_30_gt));  // open: eq, lt
  Comparator comparator_31 (.a(Player_score), .b(Win_score), .gt(comparator_31_gt), .eq(comparator_31_eq));  // open: lt
  Comparator comparator_32 (.a(Win_score), .b(Robot_score), .eq(comparator_32_eq), .lt(comparator_32_lt));  // open: gt
  not not_16 (not_16_out, multiplexer_29_out[0]);
  Multiplexer #(.width(5), .enable("false")) multiplexer_30 (
    .in0(multiplexer_25_out), .in1(multiplexer_26_out), .out(multiplexer_30_out), .sel(multiplexer_29_out[1]));
  and and_12 (Player_hit, or_4_out, comparator_27_lt, comparator_28_eq);
  and and_13 (Robot_hit, comparator_29_eq, comparator_30_gt, or_5_out);
  or or_6 (Player_win, comparator_31_gt, comparator_31_eq);
  or or_7 (Robot_win, comparator_32_eq, comparator_32_lt);
  Multiplexer #(.width(5), .enable("false")) multiplexer_31 (
    .in0(multiplexer_30_out), .in1(Robot_bat_out), .out(multiplexer_31_out), .sel(not_16_out));
  or or_8 (or_8_out, Player_hit, Robot_hit, xor_2_out);
  or or_9 (or_9_out, Player_win, Robot_win);
  Comparator comparator_33 (.a(Win_score), .b({8{1'b0}}), .gt(comparator_33_gt));  // open: eq, lt
  and and_14 (Game_status, or_9_out, comparator_33_gt);
  // NOT_Gate not_17 is placed but not wired

  // Other names for the same wires on the sheet: vXY[2:0] = vX; _5_bit_X[4:0] = ball_X; _8_bit_X[7:3] = ball_X;
  //   _5_bit_Y[4:0] = ball_Y; _8_bit_Y[7:3] = ball_Y; P_BAT[4:0] = Player_bat_out; Player_bat_move[1:0] = Joystik;
  //   R_BAT[4:0] = Robot_bat_out; RST = Reset; vY[2:0] = vXY

  // Notes on the sheet:
  //   Player bat control
  //   11 - down
  //   01 - up
  //   Ball cords Y
  //   Score
  //   Calculate vY after hit with bat
  //   How many points to win
  //   0 0 = 0; 0 1 = 1; 1 0 = 0; 1 1 = 0
  //   Vxy for chip
  //   Robot speed
  //   Robot bat control
  //   Ball cords X
  //   Game status
endmodule

module full_video_chip (
  input  [4:0] X_ball,
  input  [4:0] Y_ball,
  input  [4:0] in_3,
  input  [4:0] in_4,
  output [31:0] out_5,
  output [31:0] out_6,
  output [31:0] out_7,
  output [31:0] out_8,
  output [31:0] out_9,
  output [31:0] out_10,
  output [31:0] out_11,
  output [31:0] out_12,
  output [31:0] out_13,
  output [31:0] out_14,
  output [31:0] out_15,
  output [31:0] out_16,
  output [31:0] out_17,
  output [31:0] out_18,
  output [31:0] out_19,
  output [31:0] out_20,
  output [31:0] out_21,
  output [31:0] out_22,
  output [31:0] out_23,
  output [31:0] out_24,
  output [31:0] out_25,
  output [31:0] out_26,
  output [31:0] out_27,
  output [31:0] out_28,
  output [31:0] out_29,
  output [31:0] out_30,
  output [31:0] out_31,
  output [31:0] out_32,
  output [31:0] out_33,
  output [31:0] out_34,
  output [31:0] out_35,
  output [31:0] out_36
);

  ball_video ball_video_1 (.sequence_number({5{1'b0}}), .X_ball(X_ball), .Y_ball(Y_ball), .out_4(out_5));
  ball_video ball_video_2 (.sequence_number(5'b00001), .X_ball(X_ball), .Y_ball(Y_ball), .out_4(out_6));
  ball_video ball_video_3 (.sequence_number(5'b00010), .X_ball(X_ball), .Y_ball(Y_ball), .out_4(out_7));
  ball_video_WITH_bat ball_video_with_bat_1 (
    .in_1(5'b00011), .X_ball(X_ball), .Y_ball(Y_ball), .Y_bat(in_3), .out_5(out_8));
  ball_video ball_video_4 (.sequence_number(5'b00100), .X_ball(X_ball), .Y_ball(Y_ball), .out_4(out_9));
  ball_video ball_video_5 (.sequence_number(5'b00101), .X_ball(X_ball), .Y_ball(Y_ball), .out_4(out_10));
  ball_video ball_video_6 (.sequence_number(5'b00110), .X_ball(X_ball), .Y_ball(Y_ball), .out_4(out_11));
  ball_video ball_video_7 (.sequence_number(5'b00111), .X_ball(X_ball), .Y_ball(Y_ball), .out_4(out_12));
  ball_video ball_video_8 (.sequence_number(5'b01000), .X_ball(X_ball), .Y_ball(Y_ball), .out_4(out_13));
  ball_video ball_video_9 (.sequence_number(5'b01001), .X_ball(X_ball), .Y_ball(Y_ball), .out_4(out_14));
  ball_video ball_video_10 (.sequence_number(5'b01010), .X_ball(X_ball), .Y_ball(Y_ball), .out_4(out_15));
  ball_video ball_video_11 (.sequence_number(5'b01011), .X_ball(X_ball), .Y_ball(Y_ball), .out_4(out_16));
  ball_video ball_video_12 (.sequence_number(5'b01100), .X_ball(X_ball), .Y_ball(Y_ball), .out_4(out_17));
  ball_video ball_video_13 (.sequence_number(5'b01101), .X_ball(X_ball), .Y_ball(Y_ball), .out_4(out_18));
  ball_video ball_video_14 (.sequence_number(5'b01110), .X_ball(X_ball), .Y_ball(Y_ball), .out_4(out_19));
  ball_video ball_video_15 (.sequence_number(5'b01111), .X_ball(X_ball), .Y_ball(Y_ball), .out_4(out_20));
  ball_video ball_video_16 (.sequence_number(5'b10000), .X_ball(X_ball), .Y_ball(Y_ball), .out_4(out_21));
  ball_video ball_video_17 (.sequence_number(5'b10001), .X_ball(X_ball), .Y_ball(Y_ball), .out_4(out_22));
  ball_video ball_video_18 (.sequence_number(5'b10010), .X_ball(X_ball), .Y_ball(Y_ball), .out_4(out_23));
  ball_video ball_video_19 (.sequence_number(5'b10011), .X_ball(X_ball), .Y_ball(Y_ball), .out_4(out_24));
  ball_video ball_video_20 (.sequence_number(5'b10100), .X_ball(X_ball), .Y_ball(Y_ball), .out_4(out_25));
  ball_video ball_video_21 (.sequence_number(5'b10101), .X_ball(X_ball), .Y_ball(Y_ball), .out_4(out_26));
  ball_video ball_video_22 (.sequence_number(5'b10110), .X_ball(X_ball), .Y_ball(Y_ball), .out_4(out_27));
  ball_video ball_video_23 (.sequence_number(5'b10111), .X_ball(X_ball), .Y_ball(Y_ball), .out_4(out_28));
  ball_video ball_video_24 (.sequence_number(5'b11000), .X_ball(X_ball), .Y_ball(Y_ball), .out_4(out_29));
  ball_video ball_video_25 (.sequence_number(5'b11001), .X_ball(X_ball), .Y_ball(Y_ball), .out_4(out_30));
  ball_video ball_video_26 (.sequence_number(5'b11010), .X_ball(X_ball), .Y_ball(Y_ball), .out_4(out_31));
  ball_video ball_video_27 (.sequence_number(5'b11011), .X_ball(X_ball), .Y_ball(Y_ball), .out_4(out_32));
  ball_video_WITH_bat ball_video_with_bat_2 (
    .in_1(5'b11100), .X_ball(X_ball), .Y_ball(Y_ball), .Y_bat(in_4), .out_5(out_33));
  ball_video ball_video_28 (.sequence_number(5'b11101), .X_ball(X_ball), .Y_ball(Y_ball), .out_4(out_34));
  ball_video ball_video_29 (.sequence_number(5'b11110), .X_ball(X_ball), .Y_ball(Y_ball), .out_4(out_35));
  ball_video ball_video_30 (.sequence_number({5{1'b1}}), .X_ball(X_ball), .Y_ball(Y_ball), .out_4(out_36));

  // Notes on the sheet:
  //   Player bat
  //   Robot bat
endmodule

module ball_video (
  input  [4:0] sequence_number,
  input  [4:0] X_ball,
  input  [4:0] Y_ball,
  output [31:0] out_4
);

  wire comparator_1_eq;
  wire [31:0] decoder_1_out0;

  Comparator #(.width(5)) comparator_1 (.a(sequence_number), .b(X_ball), .eq(comparator_1_eq));  // open: gt, lt
  Decoder #(.select(5), .enable("false")) decoder_1 (
    .out0(decoder_1_out0[0]), .out1(decoder_1_out0[1]), .out2(decoder_1_out0[2]), .out3(decoder_1_out0[3]),
    .out4(decoder_1_out0[4]), .out5(decoder_1_out0[5]), .out6(decoder_1_out0[6]), .out7(decoder_1_out0[7]),
    .out8(decoder_1_out0[8]), .out9(decoder_1_out0[9]), .out10(decoder_1_out0[10]),
    .out11(decoder_1_out0[11]), .out12(decoder_1_out0[12]), .out13(decoder_1_out0[13]),
    .out14(decoder_1_out0[14]), .out15(decoder_1_out0[15]), .out16(decoder_1_out0[16]),
    .out17(decoder_1_out0[17]), .out18(decoder_1_out0[18]), .out19(decoder_1_out0[19]),
    .out20(decoder_1_out0[20]), .out21(decoder_1_out0[21]), .out22(decoder_1_out0[22]),
    .out23(decoder_1_out0[23]), .out24(decoder_1_out0[24]), .out25(decoder_1_out0[25]),
    .out26(decoder_1_out0[26]), .out27(decoder_1_out0[27]), .out28(decoder_1_out0[28]),
    .out29(decoder_1_out0[29]), .out30(decoder_1_out0[30]), .out31(decoder_1_out0[31]), .sel(Y_ball));
  Multiplexer #(.width(32), .enable("false")) multiplexer_1 (
    .in0({32{1'b0}}), .in1(decoder_1_out0), .out(out_4), .sel(comparator_1_eq));
endmodule

module ball_video_WITH_bat (
  input  [4:0] in_1,
  input  [4:0] X_ball,
  input  [4:0] Y_ball,
  input  [4:0] Y_bat,
  output [31:0] out_5
);

  wire comparator_1_eq;
  wire [31:0] decoder_1_out0, decoder_2_out0, multiplexer_1_out, shifter_1_out, shifter_2_out;

  Comparator #(.width(5)) comparator_1 (.a(in_1), .b(X_ball), .eq(comparator_1_eq));  // open: gt, lt
  Decoder #(.select(5), .enable("false")) decoder_1 (
    .out0(decoder_1_out0[0]), .out1(decoder_1_out0[1]), .out2(decoder_1_out0[2]), .out3(decoder_1_out0[3]),
    .out4(decoder_1_out0[4]), .out5(decoder_1_out0[5]), .out6(decoder_1_out0[6]), .out7(decoder_1_out0[7]),
    .out8(decoder_1_out0[8]), .out9(decoder_1_out0[9]), .out10(decoder_1_out0[10]),
    .out11(decoder_1_out0[11]), .out12(decoder_1_out0[12]), .out13(decoder_1_out0[13]),
    .out14(decoder_1_out0[14]), .out15(decoder_1_out0[15]), .out16(decoder_1_out0[16]),
    .out17(decoder_1_out0[17]), .out18(decoder_1_out0[18]), .out19(decoder_1_out0[19]),
    .out20(decoder_1_out0[20]), .out21(decoder_1_out0[21]), .out22(decoder_1_out0[22]),
    .out23(decoder_1_out0[23]), .out24(decoder_1_out0[24]), .out25(decoder_1_out0[25]),
    .out26(decoder_1_out0[26]), .out27(decoder_1_out0[27]), .out28(decoder_1_out0[28]),
    .out29(decoder_1_out0[29]), .out30(decoder_1_out0[30]), .out31(decoder_1_out0[31]), .sel(Y_ball));
  Decoder #(.select(5)) decoder_2 (
    .out0(decoder_2_out0[0]), .out1(decoder_2_out0[1]), .out2(decoder_2_out0[2]), .out3(decoder_2_out0[3]),
    .out4(decoder_2_out0[4]), .out5(decoder_2_out0[5]), .out6(decoder_2_out0[6]), .out7(decoder_2_out0[7]),
    .out8(decoder_2_out0[8]), .out9(decoder_2_out0[9]), .out10(decoder_2_out0[10]),
    .out11(decoder_2_out0[11]), .out12(decoder_2_out0[12]), .out13(decoder_2_out0[13]),
    .out14(decoder_2_out0[14]), .out15(decoder_2_out0[15]), .out16(decoder_2_out0[16]),
    .out17(decoder_2_out0[17]), .out18(decoder_2_out0[18]), .out19(decoder_2_out0[19]),
    .out20(decoder_2_out0[20]), .out21(decoder_2_out0[21]), .out22(decoder_2_out0[22]),
    .out23(decoder_2_out0[23]), .out24(decoder_2_out0[24]), .out25(decoder_2_out0[25]),
    .out26(decoder_2_out0[26]), .out27(decoder_2_out0[27]), .out28(decoder_2_out0[28]),
    .out29(decoder_2_out0[29]), .out30(decoder_2_out0[30]), .out31(decoder_2_out0[31]), .sel(Y_bat));  // open: en
  assign out_5 = multiplexer_1_out | decoder_2_out0 | shifter_1_out | shifter_2_out;  // OR_Gate or_1, 32 bits wide
  Multiplexer #(.width(32), .enable("false")) multiplexer_1 (
    .in0({32{1'b0}}), .in1(decoder_1_out0), .out(multiplexer_1_out), .sel(comparator_1_eq));
  Shifter #(.width(32)) shifter_1 (.in(decoder_2_out0), .\dist (5'b00001), .out(shifter_1_out));
  Shifter #(.width(32)) shifter_2 (.in(shifter_1_out), .\dist (5'b00001), .out(shifter_2_out));

  // Notes on the sheet:
  //   current X ball
  //   Y next
endmodule

module to_10_notation (
  input  [7:0] in_1,
  output [3:0] out_2,
  output [3:0] out_3
);

  wire [7:4] divider_1_out, divider_1_rem;

  Divider divider_1 (.a(in_1), .b(8'ha), .out({divider_1_out, out_2}), .rem({divider_1_rem, out_3}));  // open: upper
endmodule

module _8_bit_reg (
  input  [7:0] In,
  input  [7:0] Reset_value,
  input  Reset,
  input  Tacts,
  output [7:0] out
);

  wire [7:0] multiplexer_1_out;

  Multiplexer #(.width(8), .enable("false")) multiplexer_1 (
    .in0(In), .in1(Reset_value), .out(multiplexer_1_out), .sel(Reset));
  Register register_1 (.D(multiplexer_1_out), .Q(out), .clk(Tacts));  // open: en, clr
endmodule

module _5_bit_reg (
  input  [4:0] In,
  input  [4:0] Reset_value,
  input  in_3,
  input  in_4,
  output [4:0] out_5
);

  wire [4:0] multiplexer_1_out;

  Multiplexer #(.width(5), .enable("false")) multiplexer_1 (
    .in0(In), .in1(Reset_value), .out(multiplexer_1_out), .sel(in_3));
  Register #(.width(5)) register_1 (.D(multiplexer_1_out), .Q(out_5), .clk(in_4));  // open: en, clr
endmodule

module _3_bit_reg (
  input  [2:0] In,
  input  [2:0] Reset_value,
  input  in_3,
  input  in_4,
  output [2:0] out_5
);

  wire [2:0] multiplexer_1_out;

  Multiplexer #(.width(3), .enable("false")) multiplexer_1 (
    .in0(In), .in1(Reset_value), .out(multiplexer_1_out), .sel(in_3));
  Register #(.width(3)) register_1 (.D(multiplexer_1_out), .Q(out_5), .clk(in_4));  // open: en, clr
endmodule

module Robot_chip (
  input  in_1,
  input  [7:0] Vxy,
  input  [7:0] Ball_X,
  input  [7:0] Ball_Y,
  output [4:0] Ball_Y_predict
);

  wire and_1_out, and_2_out, and_3_out, and_4_out, and_5_out, and_6_out, and_7_out, cdm_8_mark5_1_p1,
       cdm_8_mark5_1_p3, cdm_8_mark5_1_p4, comparator_1_eq, comparator_2_eq, comparator_3_eq,
       comparator_4_eq, data_ins_prime, mem, not_1_out, not_2_out, not_3_out, rd_wr_prime, Restore_ans, TCT,
       undriven;
  wire [7:0] addr, cdm_8_mark5_1_p9, cdm_8_mark5_1_p10, controlled_buffer_2_out;

  // Probe on cdm_8_mark5_1_p4
  // Probe on cdm_8_mark5_1_p3
  // Probe on cdm_8_mark5_1_p1
  // Probe on nothing
  // Probe on nothing
  // Probe on nothing
  // Probe on nothing
  // CdM_8_mark5 cdm_8_mark5_1: pin names not known; wires that end beside it: cdm_8_mark5_1_p1, TCT, cdm_8_mark5_1_p3, cdm_8_mark5_1_p4, data_ins_prime, mem, rd_wr_prime, addr, cdm_8_mark5_1_p9, cdm_8_mark5_1_p10
  assign cdm_8_mark5_1_p10 = rd_wr_prime ? controlled_buffer_2_out : 8'bz;  // Controlled_Buffer controlled_buffer_1
  assign controlled_buffer_2_out = not_1_out ? cdm_8_mark5_1_p9 : 8'bz;  // Controlled_Buffer controlled_buffer_2
  not not_1 (not_1_out, rd_wr_prime);
  and and_1 (and_1_out, data_ins_prime, mem, rd_wr_prime, addr[0], ~addr[1], ~addr[2], ~addr[3]);  // AND_Gate
  // Probe on Vxy
  and and_2 (and_2_out, data_ins_prime, mem, rd_wr_prime, ~addr[0], addr[1], ~addr[2], ~addr[3]);  // AND_Gate
  and and_3 (and_3_out, data_ins_prime, mem, rd_wr_prime, addr[0], addr[1], ~addr[2], ~addr[3]);  // AND_Gate
  and and_4 (and_4_out, data_ins_prime, mem, ~rd_wr_prime, ~addr[0], ~addr[1], addr[2], ~addr[3]);  // AND_Gate
  Clock clock_1 (.out(TCT));
  Comparator #(.width(4)) comparator_1 (.a(addr[7:4]), .b(4'b1111), .eq(comparator_1_eq));  // open: gt, lt
  Comparator #(.width(4)) comparator_2 (.a(addr[7:4]), .b(4'b1111), .eq(comparator_2_eq));  // open: gt, lt
  Comparator #(.width(4)) comparator_3 (.a(addr[7:4]), .b(4'b1111), .eq(comparator_3_eq));  // open: gt, lt
  Comparator #(.width(4)) comparator_4 (.a(addr[7:4]), .b(4'b1111), .eq(comparator_4_eq));  // open: gt, lt
  not not_2 (not_2_out, data_ins_prime);
  and and_5 (and_5_out, and_1_out, comparator_1_eq);
  assign controlled_buffer_2_out = and_5_out ? Vxy : 8'bz;  // Controlled_Buffer controlled_buffer_3
  and and_6 (and_6_out, and_2_out, comparator_2_eq);
  assign controlled_buffer_2_out = and_6_out ? Ball_X : 8'bz;  // Controlled_Buffer controlled_buffer_4
  and and_7 (and_7_out, and_3_out, comparator_3_eq);
  assign controlled_buffer_2_out = and_7_out ? Ball_Y : 8'bz;  // Controlled_Buffer controlled_buffer_5
  and and_8 (Restore_ans, and_4_out, comparator_4_eq);
  ROM rom_1 (.addr(addr), .data(controlled_buffer_2_out), .sel(not_2_out));
  // Probe on controlled_buffer_2_out
  // Probe on Ball_Y_predict
  _5_bit_reg u_5_bit_reg_1 (
    .In(controlled_buffer_2_out[7:3]), .Reset_value(5'b01110), .out_5(Ball_Y_predict), .in_3(in_1),
    .in_4(not_3_out));
  not not_3 (not_3_out, Restore_ans);
  // NOT_Gate not_4 has open pins: in=undriven, out=open

  // Other names for the same wires on the sheet: addr_4_bit[3:0] = addr[3:0]; is_F[3:0] = addr[7:4]; RST = in_1

  // Notes on the sheet:
  //   contents of rom_1 (hex, n*v repeats v):
  //   cd e0 d0 f2 d1 f a1 d0 f3 d1 50 a1 d0 f1 d1 2a a1 d1 f1 b5 d0 4 41 e1 6d d1 f2 b5 d0 d0 31 91 d0 7f
  //   41 4 d1 f1 b5 91 91 91 d2 7 49 d2 4 46 e1 48 d2 f3 ba d3 0 3b e d3 0 5 ed 45 12 e3 42 8f 89 ee 3b 8
  //   ee 62 85 d2 7 49 d2 f3 ba d3 0 3e d3 0 5 ed 5e 12 e3 5b 8f 89 ee 54 d1 0 36 8 d1 1 47 e0 6a d1 0 34
  //   d1 f4 a4 ee 11 d4
  //   ВОЗМОЖНО МОЖНО УДАЛИТЬ mem и некоторые другие условия из AND
  //   (походу только mem, data/ins' удалять нельзя, начинает бред считать)
endmodule
